// Logisim project Task1.8.circ as structural Verilog: 9 circuits, main circuit CPU_main
module CPU_main (
);

  wire alu_1_acc_equal_zero, alu_1_acc_ne_zero, and_1_out, and_2_out, and_3_out, and_4_out, and_5_out,
       B1_out, B2_out, B3_out, clock_1_out, instruction_decoding_unit_1_bez,
       instruction_decoding_unit_1_bnez, instruction_decoding_unit_1_clear_tty,
       instruction_decoding_unit_1_generate_random, instruction_decoding_unit_1_jal,
       instruction_decoding_unit_1_output_char, instruction_decoding_unit_1_pointer,
       instruction_decoding_unit_1_reset_latch, instruction_decoding_unit_1_ret,
       instruction_decoding_unit_1_stop, instruction_decoding_unit_1_use_memory,
       instruction_decoding_unit_1_user_input, instruction_decoding_unit_1_write_acc,
       instruction_decoding_unit_1_write_memory, not_1_out, not_2_out, not_3_out, not_4_out, not_5_out,
       or_1_out, or_2_out, or_3_out, sr_latch_1_q, sr_latch_2_q, sr_latch_3_q;
  wire [1:0] button_press_conversion_1_out_4, select_bit_pc_1_mux_in, select_input_2_1_select_bit;
  wire [3:0] instruction_decoding_unit_1_alu_operation;
  wire [7:0] ACC_q, adder_1_out, alu_1_alu_to_acc, bit_extender_1_out, bit_extender_2_out, Data_Memory_dout,
       instruction_decoding_unit_1_addr_or_imm, LINK_REG_q, multiplexer_1_out, multiplexer_2_out,
       multiplexer_3_out, PC_q, random_1_out;
  wire [15:0] Instruction_Memory_data;

  or or_1 (or_1_out, and_1_out, and_2_out, instruction_decoding_unit_1_jal);
  and and_1 (and_1_out, alu_1_acc_ne_zero, instruction_decoding_unit_1_bnez);
  and and_2 (and_2_out, instruction_decoding_unit_1_bez, alu_1_acc_equal_zero);
  not not_1 (not_1_out, instruction_decoding_unit_1_stop);
  Clock clock_1 (.out(clock_1_out));
  SELECT_BIT_PC select_bit_pc_1 (
    .JAL_BEZ_BNEZ(or_1_out), .RET(instruction_decoding_unit_1_ret), .MUX_IN(select_bit_pc_1_mux_in));
  and and_3 (and_3_out, not_1_out, clock_1_out);
  Random random_1 (
    .next(instruction_decoding_unit_1_generate_random), .clk(and_3_out), .out(random_1_out));  // open: clr
  Adder adder_1 (.a(PC_q), .b(8'h1), .out(adder_1_out));  // open: cin, cout
  Register LINK_REG (
    .D(adder_1_out), .en(instruction_decoding_unit_1_jal), .clk(and_3_out), .Q(LINK_REG_q));  // open: clr
  Multiplexer #(.select(2), .width(8)) multiplexer_1 (
    .in0(adder_1_out), .in1(instruction_decoding_unit_1_addr_or_imm), .in2(LINK_REG_q),
    .out(multiplexer_1_out), .sel(select_bit_pc_1_mux_in));  // open: in3
  assign bit_extender_1_out = {{6{1'b0}}, random_1_out[1:0]};  // Bit_Extender bit_extender_1
  Register PC (.D(multiplexer_1_out), .clk(and_3_out), .Q(PC_q));  // open: en, clr
  Instruction_Decoding_Unit instruction_decoding_unit_1 (
    .Instruction(Instruction_Memory_data), .ALU_Operation(instruction_decoding_unit_1_alu_operation),
    .Write_ACC(instruction_decoding_unit_1_write_acc), .Use_Memory(instruction_decoding_unit_1_use_memory),
    .Write_Memory(instruction_decoding_unit_1_write_memory), .BNEZ(instruction_decoding_unit_1_bnez),
    .Output_Char(instruction_decoding_unit_1_output_char),
    .User_Input(instruction_decoding_unit_1_user_input), .BEZ(instruction_decoding_unit_1_bez),
    .RESET_LATCH(instruction_decoding_unit_1_reset_latch),
    .GENERATE_RANDOM(instruction_decoding_unit_1_generate_random),
    .CLEAR_TTY(instruction_decoding_unit_1_clear_tty), .POINTER(instruction_decoding_unit_1_pointer),
    .JAL(instruction_decoding_unit_1_jal), .RET(instruction_decoding_unit_1_ret),
    .Stop(instruction_decoding_unit_1_stop), .Addr_or_Imm(instruction_decoding_unit_1_addr_or_imm));
  Multiplexer #(.width(8)) multiplexer_2 (
    .in0(instruction_decoding_unit_1_addr_or_imm), .in1(ACC_q), .out(multiplexer_2_out),
    .sel(instruction_decoding_unit_1_pointer));
  RAM #(.asyncread("true"), .clearpin("true")) Data_Memory (
    .addr(multiplexer_2_out), .we(instruction_decoding_unit_1_write_memory), .clk(and_3_out), .din(ACC_q),
    .dout(Data_Memory_dout));  // open: oe, clr
  ROM #(.dataWidth(16)) Instruction_Memory (.addr(PC_q), .data(Instruction_Memory_data));
  or or_2 (or_2_out, instruction_decoding_unit_1_pointer, instruction_decoding_unit_1_use_memory);
  SELECT_INPUT_2 select_input_2_1 (
    .USE_MEMORY(or_2_out), .GENERATE_RANDOM(instruction_decoding_unit_1_generate_random),
    .USER_INPUT(instruction_decoding_unit_1_user_input), .SELECT_BIT(select_input_2_1_select_bit));
  Multiplexer #(.select(2), .width(8)) multiplexer_3 (
    .in0(instruction_decoding_unit_1_addr_or_imm), .in1(Data_Memory_dout), .in2(bit_extender_2_out),
    .in3(bit_extender_1_out), .out(multiplexer_3_out), .sel(select_input_2_1_select_bit));
  Register ACC (.D(alu_1_alu_to_acc), .en(or_3_out), .clk(and_3_out), .Q(ACC_q));  // open: clr
  or or_3 (or_3_out, instruction_decoding_unit_1_write_acc, instruction_decoding_unit_1_generate_random, instruction_decoding_unit_1_pointer, instruction_decoding_unit_1_user_input);
  ALU alu_1 (
    .ALU_Operation(instruction_decoding_unit_1_alu_operation), .From_ACC(ACC_q), .Input2(multiplexer_3_out),
    .ACC_EQUAL_ZERO(alu_1_acc_equal_zero), .ACC_NE_Zero(alu_1_acc_ne_zero), .ALU_to_ACC(alu_1_alu_to_acc));
  and and_4 (and_4_out, instruction_decoding_unit_1_clear_tty, and_3_out);
  TTY tty_1 (.data(ACC_q[6:0]), .clk(and_3_out), .we(instruction_decoding_unit_1_output_char), .clr(and_4_out));
  Button B1 (.out(B1_out));
  Button B2 (.out(B2_out));
  Button B3 (.out(B3_out));
  and and_5 (and_5_out, and_3_out, instruction_decoding_unit_1_reset_latch);
  not not_2 (not_2_out, B1_out);
  not not_3 (not_3_out, B2_out);
  not not_4 (not_4_out, B3_out);
  not not_5 (not_5_out, and_5_out);
  SR_LATCH sr_latch_1 (.S(not_2_out), .R(not_5_out), .Q(sr_latch_1_q));  // open: NOTQ
  SR_LATCH sr_latch_2 (.S(not_3_out), .R(not_5_out), .Q(sr_latch_2_q));  // open: NOTQ
  SR_LATCH sr_latch_3 (.S(not_4_out), .R(not_5_out), .Q(sr_latch_3_q));  // open: NOTQ
  assign bit_extender_2_out = {{6{1'b0}}, button_press_conversion_1_out_4};  // Bit_Extender bit_extender_2
  BUTTON_PRESS_CONVERSION button_press_conversion_1 (
    .ROCK(sr_latch_1_q), .PAPER(sr_latch_2_q), .SCISSORS(sr_latch_3_q),
    .out_4(button_press_conversion_1_out_4));

  // Notes on the sheet:
  //   contents of Instruction_Memory (hex, n*v repeats v):
  //   8000 1000 3000 3001 3002 3003 3004 3005 3006 3007 1008 3007 c08e 101d 3007 c08e c098 2000 1803 4068
  //   2001 1802 4068 2002 1802 4068 a000 1034 3007 c08e 1045 3007 c08e 104f 3007 c08e 105a 3007 c08e c098
  //   9000 7028 3005 2004 2905 3006 2006 1103 3006 2006 1a03 3006 a000 2006 1801 4042 2006 1802 404c 107b
  //   3007 c08e 2000 1101 3000 c056 1068 3007 c08e 2001 1101 3001 2000 1101 3000 c056 1071 3007 c08e 2002
  //   1101 3002 2000 1101 3000 c056 2003 1801 4011 a000 1088 3007 c08e 10a0 3007 c08e c098 2004 1801 7068
  //   2003 1101 3003 c011 2001 2802 4084 2001 2502 4070 1001 407a a000 10bb 3007 c08e 10de 3007 c08e c098
  //   1001 4000 a000 10cc 3007 c08e 10de 3007 c08e c098 1001 4000 a000 107b 3007 c08e 10de 3007 c08e c098
  //   1001 4000 2007 b000 7097 5000 2007 1101 3007 1001 408e d000 8000 6000 7099 3004 d000
  //   Student id: 24820129
endmodule

module Instruction_Decoding_Unit (
  input  [15:0] Instruction,
  output [3:0] ALU_Operation,
  output Write_ACC,
  output Use_Memory,
  output Write_Memory,
  output BNEZ,
  output Output_Char,
  output User_Input,
  output BEZ,
  output RESET_LATCH,
  output GENERATE_RANDOM,
  output CLEAR_TTY,
  output POINTER,
  output JAL,
  output RET,
  output Stop,
  output [7:0] Addr_or_Imm
);

  wire decoder_1_out1, decoder_1_out2;

  Decoder #(.select(4)) decoder_1 (
    .out1(decoder_1_out1), .out2(decoder_1_out2), .out3(Write_Memory), .out4(BNEZ), .out5(Output_Char),
    .out6(User_Input), .out7(BEZ), .out8(RESET_LATCH), .out9(GENERATE_RANDOM), .out10(CLEAR_TTY),
    .out11(POINTER), .out12(JAL), .out13(RET), .out15(Stop), .sel(Instruction[15:12]));  // open: out0, out14, en
  or or_1 (Write_ACC, decoder_1_out1, decoder_1_out2);
  or or_2 (Use_Memory, decoder_1_out2, Write_Memory);

  assign Addr_or_Imm = Instruction[7:0];
  assign ALU_Operation = Instruction[11:8];
endmodule

module ALU (
  input  [3:0] ALU_Operation,
  input  [7:0] From_ACC,
  input  [7:0] Input2,
  output ACC_EQUAL_ZERO,
  output ACC_NE_Zero,
  output [7:0] ALU_to_ACC
);

  wire comparator_1_gt, comparator_2_eq, comparator_4_eq;
  wire [7:0] adder_1_out, bit_extender_1_out, bit_extender_2_out, divider_1_rem, nand_1_out, or_1_out,
       shifter_1_out, subtractor_1_out;
  wire [15:0] hex_ascii_output_1_hex_val_ascii_output;

  Adder adder_1 (.a(From_ACC), .b(Input2), .out(adder_1_out));  // open: cin, cout
  assign nand_1_out = ~(From_ACC & Input2);  // NAND_Gate nand_1, 8 bits wide
  assign or_1_out = From_ACC | Input2;  // OR_Gate or_1, 8 bits wide
  Comparator #(.mode("unsigned")) comparator_1 (.a(From_ACC), .b(Input2), .gt(comparator_1_gt));  // open: eq, lt
  Comparator comparator_2 (.a(From_ACC), .b(Input2), .eq(comparator_2_eq));  // open: gt, lt
  Subtractor subtractor_1 (.a(From_ACC), .b(Input2), .out(subtractor_1_out));  // open: bin, bout
  Divider divider_1 (.a(From_ACC), .b(Input2), .rem(divider_1_rem));  // open: out, upper
  Shifter #(.shift("lr")) shifter_1 (.in(Input2), .\dist (3'b100), .out(shifter_1_out));
  assign bit_extender_1_out = {{7{1'b0}}, comparator_1_gt};  // Bit_Extender bit_extender_1
  assign bit_extender_2_out = {{7{comparator_2_eq}}, comparator_2_eq};  // Bit_Extender bit_extender_2
  HEX_ASCII_OUTPUT hex_ascii_output_1 (
    .HEX_TO_BE_CONVERTED(From_ACC), .HEX_VAL_ASCII_OUTPUT(hex_ascii_output_1_hex_val_ascii_output));
  Multiplexer #(.select(4), .width(8)) multiplexer_1 (
    .in0(Input2), .in1(adder_1_out), .in2(nand_1_out), .in3(or_1_out), .in4(shifter_1_out),
    .in5(bit_extender_1_out), .in6(hex_ascii_output_1_hex_val_ascii_output[7:0]),
    .in7(hex_ascii_output_1_hex_val_ascii_output[15:8]), .in8(bit_extender_2_out), .in9(subtractor_1_out),
    .in10(divider_1_rem), .out(ALU_to_ACC), .sel(ALU_Operation));  // open: in11, in12, in13, in14, in15
  Comparator comparator_3 (.a({8{1'b0}}), .b(From_ACC), .eq(ACC_EQUAL_ZERO));  // open: gt, lt
  Comparator #(.mode("unsigned")) comparator_4 (.a({8{1'b0}}), .b(From_ACC), .eq(comparator_4_eq));  // open: gt, lt
  not not_1 (ACC_NE_Zero, comparator_4_eq);
endmodule

module HEX_ASCII_OUTPUT (
  input  [7:0] HEX_TO_BE_CONVERTED,
  output [15:0] HEX_VAL_ASCII_OUTPUT
);

  wire comparator_1_eq, comparator_1_lt, comparator_2_eq, comparator_2_lt, or_1_out, or_2_out;
  wire [7:0] bit_extender_1_out, bit_extender_2_out, multiplexer_1_out, multiplexer_2_out;

  Comparator #(.mode("unsigned"), .width(4)) comparator_1 (
    .a(HEX_TO_BE_CONVERTED[3:0]), .b(4'b1001), .eq(comparator_1_eq), .lt(comparator_1_lt));  // open: gt
  Comparator #(.mode("unsigned"), .width(4)) comparator_2 (
    .a(HEX_TO_BE_CONVERTED[7:4]), .b(4'b1001), .eq(comparator_2_eq), .lt(comparator_2_lt));  // open: gt
  or or_1 (or_1_out, comparator_1_eq, comparator_1_lt);
  or or_2 (or_2_out, comparator_2_eq, comparator_2_lt);
  Multiplexer #(.width(8)) multiplexer_1 (.in0(8'h57), .in1(8'h30), .out(multiplexer_1_out), .sel(or_1_out));
  Multiplexer #(.width(8)) multiplexer_2 (.in0(8'h57), .in1(8'h30), .out(multiplexer_2_out), .sel(or_2_out));
  assign bit_extender_1_out = {{4{1'b0}}, HEX_TO_BE_CONVERTED[3:0]};  // Bit_Extender bit_extender_1
  assign bit_extender_2_out = {{4{1'b0}}, HEX_TO_BE_CONVERTED[7:4]};  // Bit_Extender bit_extender_2
  Adder adder_1 (.a(bit_extender_1_out), .b(multiplexer_1_out), .out(HEX_VAL_ASCII_OUTPUT[7:0]));  // open: cin, cout
  Adder adder_2 (.a(bit_extender_2_out), .b(multiplexer_2_out), .out(HEX_VAL_ASCII_OUTPUT[15:8]));  // open: cin, cout
endmodule

module USER_INPUT (
  input  B1,
  input  B2,
  input  B3,
  output [2:0] BUTTON_OUTPUT
);


  assign BUTTON_OUTPUT = {B3, B2, B1};
endmodule

module SELECT_INPUT_2 (
  input  USE_MEMORY,
  input  GENERATE_RANDOM,
  input  USER_INPUT,
  output [1:0] SELECT_BIT
);

  or or_1 (SELECT_BIT[0], USE_MEMORY, GENERATE_RANDOM);
  or or_2 (SELECT_BIT[1], GENERATE_RANDOM, USER_INPUT);
endmodule

module SR_LATCH (
  input  S,
  input  R,
  output Q,
  output NOTQ
);

  nand nand_1 (Q, S, NOTQ);
  nand nand_2 (NOTQ, Q, R);
endmodule

module BUTTON_PRESS_CONVERSION (
  input  ROCK,
  input  PAPER,
  input  SCISSORS,
  output [1:0] out_4
);

  or or_1 (out_4[0], ROCK, SCISSORS);
  or or_2 (out_4[1], PAPER, SCISSORS);
endmodule

module SELECT_BIT_PC (
  input  JAL_BEZ_BNEZ,
  input  RET,
  output [1:0] MUX_IN
);


  assign MUX_IN = {RET, JAL_BEZ_BNEZ};
endmodule
